# Fritzing sketch WeatherStation (saved by Fritzing 0.9.6b)

parts:
  ESP32_Devkit = ESP32S-HiLetgo [part_number=ESP32S-HiLetgo]
  I2C_Device_1 = Humidity Temperature Sensor SHT15
  Analog_Device_1 = Soil Moisture Sensor
  I2C_Device_2 = Humidity Temperature Sensor SHT15
  3_2V_LiFePO4 = Battery Holders [package=battery-aa-kit]

nets:
  N1: ESP32_Devkit.3.3, 3_2V_LiFePO4.+
  GND: ESP32_Devkit.GND, I2C_Device_1.SCL, Analog_Device_1.GND, I2C_Device_2.SCL, 3_2V_LiFePO4.-
  N2: ESP32_Devkit.GPIO0, Analog_Device_1.SIG
  N3: ESP32_Devkit.GPIO16, Analog_Device_1.VCC
  N4: ESP32_Devkit.GPIO5, I2C_Device_1.GND
  N5: ESP32_Devkit.GPIO19, I2C_Device_2.GND
  VCC: ESP32_Devkit.GPIO21, I2C_Device_1.VCC, I2C_Device_2.VCC
  N6: ESP32_Devkit.GPIO22, I2C_Device_1.SDA, I2C_Device_2.SDA

custom parts:
  ESP32S-HiLetgo: HiLetgo ESP-WROOM-32 ESP32 ESP-32S Development Board 2.4GHz Dual-Mode WiFi + Bluetooth Dual Cores Microcontroller The ESP32 integrated with Antenna switches, RF Balun, power amplifiers, low-noise amplifiers, filters, and management modules, and the entire solution occupies the least area of PCB. 2.4 GHz Wi-Fi plus Bluetooth dual-mode chip, with TSMC Ultra-low power consumption 40nm technology,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
